# Fritzing sketch LEDLevel_Light (saved by Fritzing 0.8.3b)
breadboards: 1

parts:
  Part1 = Arduino Uno (Rev3)
  LED1 = LED - 5mm [color="Red (633nm)" package="5 mm [THT]"]
  LED2 = LED - 5mm [color="Red (633nm)" package="5 mm [THT]"]
  LED3 = LED - 5mm [color="Yellow (585nm)" package="5 mm [THT]"]
  LED4 = LED - 5mm [color="Yellow (585nm)" package="5 mm [THT]"]
  LED5 = LED - 5mm [color="Green (555nm)" package="5 mm [THT]"]
  LED6 = LED - 5mm [color="Green (555nm)" package="5 mm [THT]"]
  LED7 = LED - 5mm [color="Green (555nm)" package="5 mm [THT]"]
  LED8 = LED - 5mm [color="Green (555nm)" package="5 mm [THT]"]
  R1 = Resistor [tolerance=±1% resistance=220 package=THT]
  R2 = Resistor [tolerance=±1% resistance=220 package=THT]
  R3 = Resistor [tolerance=±1% resistance=220 package=THT]
  R4 = Resistor [tolerance=±2% resistance=220 package=THT]
  R5 = Resistor [tolerance=±1% resistance=220 package=THT]
  R6 = Resistor [tolerance=±1% resistance=220 package=THT]
  R7 = Resistor [tolerance=±1% resistance=220 package=THT]
  R8 = Resistor [tolerance=±1% resistance=220 package=THT]
  Q1 = NPN-Transistor [package="TO92 [THT]"]
  Q2 = NPN-Transistor [package="TO92 [THT]"]
  R9 = Resistor [tolerance=±2% resistance=100 package=THT]
  LED9 = LED - 5mm [color="Red (633nm)" package="5 mm [THT]"]
  LED10 = LED - 5mm [color="Green (555nm)" package="5 mm [THT]"]

nets:
  N1: Part1.A0, Q2.E, R9.Pin_0
  N2: Part1.GND, R1.Pin_1, R2.Pin_1, R3.Pin_1, R4.Pin_1, R5.Pin_1, R6.Pin_1, R7.Pin_1, R8.Pin_1, R9.Pin_1
  N3: Part1.D8, LED2.anode
  N4: Part1.D9_PWM, LED1.anode
  N5: Part1.AREF, Q1.C, Q2.C
  N6: Part1.D2, LED8.anode
  N7: Part1.D3_PWM, LED7.anode
  N8: Part1.D4, LED6.anode
  N9: Part1.D5_PWM, LED5.anode
  N10: Part1.D6_PWM, LED4.anode
  N11: Part1.D7, LED3.anode
  N12: LED1.cathode, R1.Pin_0
  N13: LED2.cathode, R2.Pin_0
  N14: LED3.cathode, R3.Pin_0
  N15: LED4.cathode, R4.Pin_0
  N16: LED5.cathode, R5.Pin_0
  N17: LED6.cathode, R6.Pin_0
  N18: LED7.cathode, R7.Pin_0
  N19: LED8.cathode, R8.Pin_0
  N20: Q1.E, Q2.B, LED9.cathode, LED10.cathode
  N21: Q1.B, LED9.anode
