# Fritzing sketch blinky (saved by Fritzing 0.7.12b)
breadboards: 1

parts:
  R1 = Resistor [tolerance=±5% resistance=220 part_number=220Ω package=THT]
  LED1 = LED - 5mm [color="Red (633nm)" package="5 mm [THT]"]
  Arduino = Arduino [part_number="UNO R3"]

nets:
  N1: R1.Pin_0, LED1.cathode
  N2: R1.Pin_1, Arduino.GND
  N3: LED1.anode, Arduino.D13
